// Logisim project Hangman_Circuit.circ as structural Verilog: 17 circuits, main circuit main
module main (
);

  wire A_out, Any_matches, B_out, button_1_out, button_2_out, button_pressed, C_out, cdm_8_1_p2, cdm_8_1_p4,
       cdm_8_1_p5, cdm_8_1_p6, cdm_8_1_p7, cdm_8_1_p8, cdm_8_1_p9, cdm_8_1_p10, Clock, code, D_out, data,
       decoder_2_out0, decoder_2_out1, decoder_3_out0, decoder_3_out1, decoder_4_out0, decoder_4_out1,
       decoder_5_out0, E_out, end_game, F_out, G_out, H_out, I_Osel, I_out, In_out_prime, IO_F1_2_out,
       IO_F1_out, IO_F9_out, IO_FA_out, IO_FF_out, J_out, K_out, L_out, lose, M_out, mem, N_out, nand_1_out,
       new_game, no, not_1_out, not_2_out, O_out, P_out, panel_1_out_38, panel_1_out_39, panel_1_out_40,
       panel_1_out_41, panel_1_out_42, panel_1_out_43, panel_1_out_44, panel_1_out_45, panel_1_out_46,
       panel_1_out_47, panel_1_out_56, panel_1_out_57, panel_1_out_58, panel_1_out_59, panel_1_out_60,
       panel_1_out_67, panel_1_out_68, panel_1_out_69, panel_1_out_70, panel_1_out_71, panel_1_out_72,
       panel_1_out_73, panel_1_out_74, panel_1_out_75, panel_1_out_76, panel_1_out_77, panel_1_out_93,
       panel_1_out_94, Q_out, R_2_out, RAM, Reset, S_out, start, stop, T_out, Tick_TTY, U_out, V_out, W_out,
       win, X_out, xor_1_out, Y_out, yes, Z_out;
  wire [3:0] I_Oadr, panel_1_out_78, panel_1_out_79, register_1_q, register_1_q_2, wrong_guesses;
  wire [6:0] bit_extender_1_out, letter_code, letter_display_driver_1_col_0_out,
       letter_display_driver_1_col_1_out, letter_display_driver_1_col_2_out,
       letter_display_driver_1_col_3_out, letter_display_driver_1_col_4_out,
       letter_display_driver_2_col_0_out, letter_display_driver_2_col_1_out,
       letter_display_driver_2_col_2_out, letter_display_driver_2_col_3_out,
       letter_display_driver_2_col_4_out, letter_display_driver_3_col_0_out,
       letter_display_driver_3_col_1_out, letter_display_driver_3_col_2_out,
       letter_display_driver_3_col_3_out, letter_display_driver_3_col_4_out,
       letter_display_driver_4_col_0_out, letter_display_driver_4_col_1_out,
       letter_display_driver_4_col_2_out, letter_display_driver_4_col_3_out,
       letter_display_driver_4_col_4_out, letter_display_driver_5_col_0_out,
       letter_display_driver_5_col_1_out, letter_display_driver_5_col_2_out,
       letter_display_driver_5_col_3_out, letter_display_driver_5_col_4_out,
       letter_display_driver_6_col_0_out, letter_display_driver_6_col_1_out,
       letter_display_driver_6_col_2_out, letter_display_driver_6_col_3_out,
       letter_display_driver_6_col_4_out, letter_display_driver_7_col_0_out,
       letter_display_driver_7_col_1_out, letter_display_driver_7_col_2_out,
       letter_display_driver_7_col_3_out, letter_display_driver_7_col_4_out,
       letter_display_driver_8_col_0_out, letter_display_driver_8_col_1_out,
       letter_display_driver_8_col_2_out, letter_display_driver_8_col_3_out,
       letter_display_driver_8_col_4_out, new_word_1_letter_0, new_word_1_letter_1, new_word_1_letter_2,
       new_word_1_letter_3, new_word_1_letter_4, new_word_1_letter_5, new_word_1_letter_6,
       new_word_1_letter_7, panel_1_out_82, panel_1_out_83, panel_1_out_84, panel_1_out_85, panel_1_out_86,
       panel_1_out_87, panel_1_out_88, panel_1_out_89, panel_1_out_92, to_tty;
  wire [7:0] bit_extender_2_out, cdm_8_1_p14, cdm_8_1_p15, correct_patern, I_Odat, \matches , register_2_q,
       register_4_q, register_5_q;
  wire [7:4] cdm_8_1_p13;
  wire [7:7] win_loss, Yes_No;
  wire [15:0] panel_1_out_48, panel_1_out_49, panel_1_out_50, panel_1_out_51, panel_1_out_52, panel_1_out_53,
       panel_1_out_54, panel_1_out_55, panel_1_out_61, panel_1_out_62, panel_1_out_63, panel_1_out_64,
       panel_1_out_65, panel_1_out_66;

  // Probe on cdm_8_1_p2
  Clock clock_1 (.out(Clock));
  Button R (.out(Reset));
  // Probe on cdm_8_1_p4
  // Probe on cdm_8_1_p6
  // Probe on cdm_8_1_p5
  and and_1 (I_Osel, not_1_out, Clock, data);
  LED led_1 (.in(panel_1_out_38));
  Button A (.out(A_out));
  LED led_2 (.in(panel_1_out_43));
  Button F (.out(F_out));
  LED led_3 (.in(panel_1_out_56));
  Button K (.out(K_out));
  LED led_4 (.in(panel_1_out_67));
  Button P (.out(P_out));
  LED led_5 (.in(panel_1_out_72));
  Button U (.out(U_out));
  // Probe on cdm_8_1_p7
  // Probe on cdm_8_1_p8
  not not_1 (not_1_out, nand_1_out);
  Letter_Display_Driver letter_display_driver_1 (
    .Col_0_out(letter_display_driver_1_col_0_out), .Col_1_out(letter_display_driver_1_col_1_out),
    .Col_2_out(letter_display_driver_1_col_2_out), .Col_3_out(letter_display_driver_1_col_3_out),
    .Col_4_out(letter_display_driver_1_col_4_out), .ASCII_code_in(panel_1_out_82));
  Letter_Display_Driver letter_display_driver_2 (
    .Col_0_out(letter_display_driver_2_col_0_out), .Col_1_out(letter_display_driver_2_col_1_out),
    .Col_2_out(letter_display_driver_2_col_2_out), .Col_3_out(letter_display_driver_2_col_3_out),
    .Col_4_out(letter_display_driver_2_col_4_out), .ASCII_code_in(panel_1_out_89));
  DotMatrix dotmatrix_1 (
    .col0(letter_display_driver_1_col_0_out), .col1(letter_display_driver_1_col_1_out),
    .col2(letter_display_driver_1_col_2_out), .col3(letter_display_driver_1_col_3_out),
    .col4(letter_display_driver_1_col_4_out));
  DotMatrix dotmatrix_2 (
    .col0(letter_display_driver_2_col_0_out), .col1(letter_display_driver_2_col_1_out),
    .col2(letter_display_driver_2_col_2_out), .col3(letter_display_driver_2_col_3_out),
    .col4(letter_display_driver_2_col_4_out));
  LED led_6 (.in(panel_1_out_39));
  Button B (.out(B_out));
  LED led_7 (.in(panel_1_out_44));
  Button G (.out(G_out));
  LED led_8 (.in(panel_1_out_57));
  Button L (.out(L_out));
  LED led_9 (.in(panel_1_out_68));
  Button Q (.out(Q_out));
  LED led_10 (.in(panel_1_out_73));
  Button V (.out(V_out));
  // Probe on cdm_8_1_p9
  // CdM_8 cdm_8_1: pin names not known; wires that end beside it: Clock, cdm_8_1_p2, Reset, cdm_8_1_p4, cdm_8_1_p5, cdm_8_1_p6, cdm_8_1_p7, cdm_8_1_p8, cdm_8_1_p9, cdm_8_1_p10, mem, In_out_prime, {cdm_8_1_p13, I_Oadr}, cdm_8_1_p14, cdm_8_1_p15
  nand nand_1 (nand_1_out, cdm_8_1_p13[4], cdm_8_1_p13[5], cdm_8_1_p13[6], cdm_8_1_p13[7]);
  and and_2 (RAM, nand_1_out, data);
  DotMatrix dotmatrix_3 (
    .col0(letter_display_driver_3_col_0_out), .col1(letter_display_driver_3_col_1_out),
    .col2(letter_display_driver_3_col_2_out), .col3(letter_display_driver_3_col_3_out),
    .col4(letter_display_driver_3_col_4_out));
  Letter_Display_Driver letter_display_driver_3 (
    .Col_0_out(letter_display_driver_3_col_0_out), .Col_1_out(letter_display_driver_3_col_1_out),
    .Col_2_out(letter_display_driver_3_col_2_out), .Col_3_out(letter_display_driver_3_col_3_out),
    .Col_4_out(letter_display_driver_3_col_4_out), .ASCII_code_in(panel_1_out_83));
  LED led_11 (.in(panel_1_out_41));
  LED led_12 (.in(panel_1_out_40));
  Button D (.out(D_out));
  Button C (.out(C_out));
  LED led_13 (.in(panel_1_out_45));
  LED led_14 (.in(panel_1_out_46));
  Button H (.out(H_out));
  Button I (.out(I_out));
  LED led_15 (.in(panel_1_out_58));
  LED led_16 (.in(panel_1_out_59));
  Button N (.out(N_out));
  Button M (.out(M_out));
  LED led_17 (.in(panel_1_out_69));
  LED led_18 (.in(panel_1_out_70));
  Button S (.out(S_out));
  Button R_2 (.out(R_2_out));
  LED led_19 (.in(panel_1_out_74));
  LED led_20 (.in(panel_1_out_75));
  Button X (.out(X_out));
  Button W (.out(W_out));
  New_Word new_word_1 (
    .Clock(Clock), .New_Game(new_game), .Letter_0(new_word_1_letter_0), .Letter_1(new_word_1_letter_1),
    .Letter_2(new_word_1_letter_2), .Letter_3(new_word_1_letter_3), .Letter_4(new_word_1_letter_4),
    .Letter_5(new_word_1_letter_5), .Letter_6(new_word_1_letter_6), .Letter_7(new_word_1_letter_7));
  Decoder #(.disabled(0)) decoder_1 (.out0(code), .out1(data), .sel(cdm_8_1_p10), .en(mem));
  assign I_Odat = not_2_out ? cdm_8_1_p14 : 8'bz;  // Controlled_Buffer controlled_buffer_1
  not not_2 (not_2_out, In_out_prime);
  assign cdm_8_1_p15 = In_out_prime ? I_Odat : 8'bz;  // Controlled_Buffer controlled_buffer_2
  DotMatrix dotmatrix_4 (
    .col0(letter_display_driver_4_col_0_out), .col1(letter_display_driver_4_col_1_out),
    .col2(letter_display_driver_4_col_2_out), .col3(letter_display_driver_4_col_3_out),
    .col4(letter_display_driver_4_col_4_out));
  Letter_Display_Driver letter_display_driver_4 (
    .Col_0_out(letter_display_driver_4_col_0_out), .Col_1_out(letter_display_driver_4_col_1_out),
    .Col_2_out(letter_display_driver_4_col_2_out), .Col_3_out(letter_display_driver_4_col_3_out),
    .Col_4_out(letter_display_driver_4_col_4_out), .ASCII_code_in(panel_1_out_84));
  LED led_21 (.in(panel_1_out_42));
  Button E (.out(E_out));
  LED led_22 (.in(panel_1_out_47));
  Button J (.out(J_out));
  LED led_23 (.in(panel_1_out_60));
  panel panel_1 (
    .out_38(panel_1_out_38), .out_39(panel_1_out_39), .out_40(panel_1_out_40), .out_41(panel_1_out_41),
    .out_42(panel_1_out_42), .in_1(A_out), .in_2(B_out), .in_3(C_out), .in_4(D_out), .in_5(E_out),
    .out_43(panel_1_out_43), .out_44(panel_1_out_44), .out_45(panel_1_out_45), .out_46(panel_1_out_46),
    .out_47(panel_1_out_47), .in_6(F_out), .in_7(G_out), .in_8(H_out), .in_9(I_out), .in_10(J_out),
    .out_56(panel_1_out_56), .out_57(panel_1_out_57), .out_58(panel_1_out_58), .out_59(panel_1_out_59),
    .out_60(panel_1_out_60), .in_11(K_out), .in_12(L_out), .in_13(M_out), .in_14(N_out), .in_15(O_out),
    .out_67(panel_1_out_67), .out_68(panel_1_out_68), .out_69(panel_1_out_69), .out_70(panel_1_out_70),
    .out_71(panel_1_out_71), .in_16(P_out), .in_17(Q_out), .in_18(R_2_out), .in_19(S_out), .in_20(T_out),
    .out_72(panel_1_out_72), .out_73(panel_1_out_73), .out_74(panel_1_out_74), .out_75(panel_1_out_75),
    .out_76(panel_1_out_76), .out_77(panel_1_out_77), .in_21(U_out), .in_22(V_out), .in_23(W_out),
    .in_24(X_out), .in_25(Y_out), .in_26(Z_out), .new_game(new_game), .stop(stop),
    .buttoon_pressed(button_pressed), .letter_code(letter_code), .END_GAME(end_game),
    .WRONG_GUESSES(wrong_guesses), .out_55(panel_1_out_55), .out_48(panel_1_out_48), .out_49(panel_1_out_49),
    .out_50(panel_1_out_50), .out_51(panel_1_out_51), .out_52(panel_1_out_52), .out_53(panel_1_out_53),
    .out_54(panel_1_out_54), .out_61(panel_1_out_61), .out_62(panel_1_out_62), .out_63(panel_1_out_63),
    .out_64(panel_1_out_64), .out_65(panel_1_out_65), .out_66(panel_1_out_66), .out_89(panel_1_out_89),
    .out_82(panel_1_out_82), .out_83(panel_1_out_83), .out_84(panel_1_out_84), .out_85(panel_1_out_85),
    .out_86(panel_1_out_86), .out_87(panel_1_out_87), .out_88(panel_1_out_88), .Matches(\matches ),
    .out_78(panel_1_out_78), .out_79(panel_1_out_79), .Correct_pattern(correct_patern),
    .out_92(panel_1_out_92), .TTY(to_tty), .tick_TTY(Tick_TTY), .out_93(panel_1_out_93),
    .out_94(panel_1_out_94), .yes_button(button_2_out), .YES(yes), .no_button(button_1_out), .LOSES(lose),
    .WIN(win), .NO(no), .START_prime(start));
  Button O (.out(O_out));
  LED led_24 (.in(panel_1_out_71));
  Button T (.out(T_out));
  LED led_25 (.in(panel_1_out_76));
  Button Y (.out(Y_out));
  Find_Matches find_matches_1 (
    .Letter_0(new_word_1_letter_0), .Letter_1(new_word_1_letter_1), .Letter_2(new_word_1_letter_2),
    .Letter_3(new_word_1_letter_3), .Letter_4(new_word_1_letter_4), .Letter_5(new_word_1_letter_5),
    .Letter_6(new_word_1_letter_6), .Letter_7(new_word_1_letter_7), .Letter_code(letter_code),
    .Matches(\matches ), .any_matches(Any_matches));
  // Probe on {cdm_8_1_p13, I_Oadr}
  Letter_Display_Driver letter_display_driver_5 (
    .Col_0_out(letter_display_driver_5_col_0_out), .Col_1_out(letter_display_driver_5_col_1_out),
    .Col_2_out(letter_display_driver_5_col_2_out), .Col_3_out(letter_display_driver_5_col_3_out),
    .Col_4_out(letter_display_driver_5_col_4_out), .ASCII_code_in(panel_1_out_85));
  DotMatrix dotmatrix_5 (
    .col0(letter_display_driver_5_col_0_out), .col1(letter_display_driver_5_col_1_out),
    .col2(letter_display_driver_5_col_2_out), .col3(letter_display_driver_5_col_3_out),
    .col4(letter_display_driver_5_col_4_out));
  DotMatrix #(.matrixcols(14), .matrixrows(16)) dotmatrix_6 (
    .col0(panel_1_out_55), .col1(panel_1_out_48), .col2(panel_1_out_49), .col3(panel_1_out_50),
    .col4(panel_1_out_51), .col5(panel_1_out_52), .col6(panel_1_out_53), .col7(panel_1_out_54),
    .col8(panel_1_out_61), .col9(panel_1_out_62), .col10(panel_1_out_63), .col11(panel_1_out_64),
    .col12(panel_1_out_65), .col13(panel_1_out_66));
  LED led_26 (.in(panel_1_out_77));
  Button Z (.out(Z_out));
  DotMatrix dotmatrix_7 (
    .col0(letter_display_driver_6_col_0_out), .col1(letter_display_driver_6_col_1_out),
    .col2(letter_display_driver_6_col_2_out), .col3(letter_display_driver_6_col_3_out),
    .col4(letter_display_driver_6_col_4_out));
  Letter_Display_Driver letter_display_driver_6 (
    .Col_0_out(letter_display_driver_6_col_0_out), .Col_1_out(letter_display_driver_6_col_1_out),
    .Col_2_out(letter_display_driver_6_col_2_out), .Col_3_out(letter_display_driver_6_col_3_out),
    .Col_4_out(letter_display_driver_6_col_4_out), .ASCII_code_in(panel_1_out_86));
  Hex_Digit_Display hex_digit_display_1 (.value(panel_1_out_78));  // open: dp
  Hex_Digit_Display hex_digit_display_2 (.value(panel_1_out_79));  // open: dp
  ROM rom_1 (.addr({cdm_8_1_p13, I_Oadr}), .data(I_Odat), .sel(code));
  RAM ram_1 (.addr({cdm_8_1_p13, I_Oadr}), .data(I_Odat), .sel(RAM), .clk(Clock), .ld(In_out_prime));  // open: clr
  DotMatrix dotmatrix_8 (
    .col0(letter_display_driver_7_col_0_out), .col1(letter_display_driver_7_col_1_out),
    .col2(letter_display_driver_7_col_2_out), .col3(letter_display_driver_7_col_3_out),
    .col4(letter_display_driver_7_col_4_out));
  Letter_Display_Driver letter_display_driver_7 (
    .Col_0_out(letter_display_driver_7_col_0_out), .Col_1_out(letter_display_driver_7_col_1_out),
    .Col_2_out(letter_display_driver_7_col_2_out), .Col_3_out(letter_display_driver_7_col_3_out),
    .Col_4_out(letter_display_driver_7_col_4_out), .ASCII_code_in(panel_1_out_87));
  TTY #(.rows(10), .cols(40)) tty_1 (.data(panel_1_out_92), .clk(panel_1_out_93), .clr(panel_1_out_94));  // open: we
  wrong_guesses wrong_guesses_1 (
    .wrong_guesses(wrong_guesses), .end_game(end_game), .button_pressed(button_pressed),
    .any_matches(Any_matches), .new_game(new_game));
  correct_pattern correct_pattern_1 (
    .correct_pattern(correct_patern), .\matches (\matches ), .end_game(end_game), .button_pressed(xor_1_out),
    .new_game(new_game));
  xor xor_1 (xor_1_out, new_game, button_pressed);
  DotMatrix dotmatrix_9 (
    .col0(letter_display_driver_8_col_0_out), .col1(letter_display_driver_8_col_1_out),
    .col2(letter_display_driver_8_col_2_out), .col3(letter_display_driver_8_col_3_out),
    .col4(letter_display_driver_8_col_4_out));
  Letter_Display_Driver letter_display_driver_8 (
    .Col_0_out(letter_display_driver_8_col_0_out), .Col_1_out(letter_display_driver_8_col_1_out),
    .Col_2_out(letter_display_driver_8_col_2_out), .Col_3_out(letter_display_driver_8_col_3_out),
    .Col_4_out(letter_display_driver_8_col_4_out), .ASCII_code_in(panel_1_out_88));
  Button button_1 (.out(button_1_out));
  Button button_2 (.out(button_2_out));
  ROM rom_2 ();  // open: addr, data, sel
  Comparator #(.width(4), .mode("unsigned")) comparator_1 (.a(wrong_guesses), .b(4'b1100), .eq(lose));  // open: gt, lt
  Comparator #(.mode("unsigned")) comparator_2 (.a(correct_patern), .b({8{1'b1}}), .eq(win));  // open: gt, lt
  xor xor_2 (stop, lose, win);
  Bit_Extender #(.out_width(7)) bit_extender_1 (.in({register_1_q_2, register_1_q}), .out(bit_extender_1_out));
  Hex_Digit_Display hex_digit_display_3 (.value(register_1_q));  // open: dp
  Hex_Digit_Display hex_digit_display_4 (.value(register_1_q_2));  // open: dp
  Register #(.trigger("falling")) register_1 (
    .D(I_Odat), .en(decoder_2_out0), .Q({register_1_q_2, register_1_q}), .clk(I_Osel));  // open: clr
  assign bit_extender_2_out = {{1{1'b0}}, letter_code};  // Bit_Extender bit_extender_2
  and IO_F1 (IO_F1_out, ~I_Oadr[0], ~I_Oadr[1], ~I_Oadr[2], ~I_Oadr[3], I_Osel);  // AND_Gate
  Decoder #(.disabled(0)) decoder_2 (.out0(decoder_2_out0), .out1(decoder_2_out1), .sel(In_out_prime), .en(IO_F1_out));
  Register #(.trigger("high")) register_2 (
    .D(bit_extender_2_out), .Q(register_2_q), .clk(button_pressed));  // open: en, clr
  assign I_Odat = decoder_2_out1 ? register_2_q : 8'bz;  // Controlled_Buffer controlled_buffer_3
  Register #(.trigger("falling")) register_3 (.D(I_Odat), .clk(decoder_3_out0));  // open: en, Q, clr
  assign I_Odat = decoder_3_out1 ? {win_loss[7], {5{1'b0}}, lose, win} : 8'bz;  // Controlled_Buffer controlled_buffer_4
  Register #(.trigger("falling")) register_4 (
    .D(I_Odat), .en(decoder_4_out0), .Q(register_4_q), .clk(I_Osel));  // open: clr
  assign I_Odat = decoder_4_out1 ? {Yes_No[7], {5{1'b0}}, no, yes} : 8'bz;  // Controlled_Buffer controlled_buffer_5
  Register #(.trigger("falling")) register_5 (
    .D(I_Odat), .en(decoder_5_out0), .Q(register_5_q), .clk(I_Osel));  // open: clr
  and IO_F9 (IO_F9_out, I_Osel, I_Oadr[0], ~I_Oadr[1], ~I_Oadr[2], I_Oadr[3]);  // AND_Gate
  Decoder #(.disabled(0)) decoder_3 (.out0(decoder_3_out0), .out1(decoder_3_out1), .sel(In_out_prime), .en(IO_F9_out));
  and IO_FA (IO_FA_out, I_Osel, ~I_Oadr[0], I_Oadr[1], ~I_Oadr[2], I_Oadr[3]);  // AND_Gate
  Bit_Extender #(.out_width(1)) bit_extender_3 (.in(register_4_q), .out(start));
  Decoder #(.disabled(0)) decoder_4 (.out0(decoder_4_out0), .out1(decoder_4_out1), .sel(In_out_prime), .en(IO_FA_out));
  and IO_F1_2 (IO_F1_2_out, I_Osel, I_Oadr[0], ~I_Oadr[1], ~I_Oadr[2], ~I_Oadr[3]);  // AND_Gate
  Bit_Extender #(.out_width(7)) bit_extender_4 (.in(register_5_q), .out(to_tty));
  Decoder #(.disabled(0)) decoder_5 (.out0(decoder_5_out0), .sel(In_out_prime), .en(IO_F1_2_out));  // open: out1
  and IO_FF (IO_FF_out, I_Osel, I_Oadr[0], I_Oadr[1], I_Oadr[2], I_Oadr[3]);
  Decoder #(.disabled(0)) decoder_6 (.out0(Tick_TTY), .sel(In_out_prime), .en(IO_FF_out));  // open: out1
  or or_1 (Yes_No[7], yes, no);
  or or_2 (win_loss[7], win, lose);

  // Other names for the same wires on the sheet: rd_wr_prime = In_out_prime; win_loss[1:0] = {lose, win};
  //   Yes_No[1:0] = {no, yes}

  // Notes on the sheet:
  //   memory-mapped I/O
  //   LOSSES
  //   WINS
  //   instr memory
  //   contents of rom_1 (hex, n*v repeats v):
  //   d0 a0 b1 5 e0 11 d2 f1 a9 d3 ff d2 1 ae 8c ee 2 d0 fa d1 1 a1 d1 0 a1 35 30 d0 f9 b1 5 e4 23 ee 1b
  //   d3 81 77 e1 39 d0 b4 b1 5 e0 39 d2 f1 a9 d3 ff d2 1 ae 8c ee 2a d3 82 77 e1 4f d0 c1 b1 5 e0 4f d2
  //   f1 a9 d3 ff d2 1 ae 8c ee 40 d0 cf b1 5 e0 60 d2 f1 a9 d3 ff d2 1 ae 8c ee 51 d0 fa b1 5 e4 68 ee 60
  //   d3 81 77 e1 73 30 35 3a 3f ee 1b d3 82 76 e1 7a ee 7a d3 82 77 e1 91 d0 98 b1 5 e0 90 d2 f1 a9 d3 ff
  //   d2 1 ae 8c ee 81 d4
  //   data memory
  //   I/O bus
  //   NO
  //   YES
  //   contents of rom_2 (hex, n*v repeats v):
  //   cd f0 d0 f0 b2 a e1 8 76 e0 d a2 9 ee 4 74 65 73 74 65
endmodule

module Random_Number_Generator (
  input  Clock,
  input  New_Game,
  output [8:0] Random_Number
);

  wire [8:0] random_1_out;

  Random #(.width(9)) random_1 (.clk(Clock), .out(random_1_out));  // open: next, clr
  Register #(.width(9)) register_1 (.D(random_1_out), .en(New_Game), .Q(Random_Number), .clk(Clock));  // open: clr
  // Probe on Random_Number
endmodule

module New_Word (
  input  Clock,
  input  New_Game,
  output [6:0] Letter_0,
  output [6:0] Letter_1,
  output [6:0] Letter_2,
  output [6:0] Letter_3,
  output [6:0] Letter_4,
  output [6:0] Letter_5,
  output [6:0] Letter_6,
  output [6:0] Letter_7
);

  wire [8:0] random_number_generator_1_random_number;
  wire [31:7] rom_1_data, rom_2_data;

  Random_Number_Generator random_number_generator_1 (
    .Clock(Clock), .New_Game(New_Game), .Random_Number(random_number_generator_1_random_number));
  ROM #(.addrWidth(9), .dataWidth(32)) rom_1 (
    .addr(random_number_generator_1_random_number),
    .data({rom_1_data[31], Letter_4, rom_1_data[23], Letter_5, rom_1_data[15], Letter_6, rom_1_data[7], Letter_7}));  // open: sel
  ROM #(.addrWidth(9), .dataWidth(32)) rom_2 (
    .addr(random_number_generator_1_random_number),
    .data({rom_2_data[31], Letter_0, rom_2_data[23], Letter_1, rom_2_data[15], Letter_2, rom_2_data[7], Letter_3}));  // open: sel
  // Probe on Letter_7
  // Probe on Letter_6
  // Probe on Letter_5
  // Probe on Letter_4
  // Probe on Letter_3
  // Probe on Letter_2
  // Probe on Letter_1
  // Probe on Letter_0

  // Notes on the sheet:
  //   letters 4-7
  //   letters 0-3
  //   contents of rom_1 (hex, n*v repeats v):
  //   545f5f5f 49455f5f 415f5f5f 55494e5f 485f5f5f 455f5f5f 41475f5f 5f5f5f5f 45445f5f 454c5f5f 5f5f5f5f
  //   4553535f 45465f5f 445f5f5f 52545f5f 505f5f5f 49435f5f 445f5f5f 595f5f5f 4f545f5f 4b5f5f5f 4445445f
  //   414c4c59 4e5f5f5f 455f5f5f 49455f5f 49415f5f 524f575f 445f5f5f 42414c4c 4f47595f 4c494e47 545f5f5f
  //   435f5f5f 5f5f5f5f 4b454e5f 42454c4c 484f4c45 4f575f5f 5f5f5f5f 5f5f5f5f 5445445f 4c5f5f5f 504f4e47
  //   45545f5f 5445445f 5f5f5f5f 595f5f5f 455f5f5f 45414c5f 5f5f5f5f 545f5f5f 544c455f 4154455f 455f5f5f
  //   544f574c 545f5f5f 5f5f5f5f 45525f5f 5f5f5f5f 53455f5f 455f5f5f 4f575f5f 4f415244 5f5f5f5f 545f5f5f
  //   4c45525f 454c5f5f 5349435f 5f5f5f5f 49455f5f 5f5f5f5f 4553545f 4f5f5f5f 454c5f5f 48454e5f 45545f5f
  //   5f5f5f5f 554d5f5f 5f5f5f5f 455f5f5f 5f5f5f5f 4e43595f 54494e47 4845535f 5f5f5f5f 455f5f5f 5541545f
  //   415f5f5f 5f5f5f5f 4147455f 4c455f5f 45455f5f 5f5f5f5f 53485f5f 53555246 4154455f 455f5f5f 45545441
  //   4c455f5f 54414e54 545f5f5f 4d5f5f5f 5f5f5f5f 4c455f5f 53455f5f 41494e5f 4e475f5f 4f44494c 5f5f5f5f
  //   4741525f 4845545f 5f5f5f5f 5f5f5f5f 4449414e 535f5f5f 44455f5f 5f5f5f5f 4f575f5f 48545f5f 41545f5f
  //   5f5f5f5f 455f5f5f 4d414e5f 43545f5f 5f5f5f5f 494e475f 45525f5f 4154455f 53455f5f 4f575f5f 5354595f
  //   4543545f 53455f5f 45525f5f 5f5f5f5f 4748545f 4c5f5f5f 5f5f5f5f 4e475f5f 4954455f 455f5f5f 4c455353
  //   4e47595f 53545f5f 465f5f5f 485f5f5f 4e475f5f 4154455f 5f5f5f5f 52445f5f 5f5f5f5f 43545f5f 4953485f
  //   4f434b5f 5f5f5f5f 4c4f5553 49415445 4f4d5f5f 4f4e5f5f 5f5f5f5f 5445535f 5f5f5f5f 4c455353 5f5f5f5f
  //   5f5f5f5f 4c455f5f 54434150 4c455f5f 5f5f5f5f 454e5f5f 4d41535f 414c5f5f 465f5f5f 4c454e5f 4d494e47
  //   485f5f5f 4c5f5f5f 574f4f44 494e475f 45545f5f 4f505f5f 45525345 50494e47 5f5f5f5f 49504f50 454c4c41
  //   534f5253 485f5f5f 5f5f5f5f 554c5f5f 45535f5f 535f5f5f 5f5f5f5f 4f4e5f5f 535f5f5f 48545f5f 5f5f5f5f
  //   4f494c54 4e535f5f 464c4f50 4c5f5f5f 45545f5f 455f5f5f 545f5f5f 5f5f5f5f 454e545f 44415244 545f5f5f
  //   4c455f5f 45524552 4f52545f 545f5f5f 4c455f5f 544c455f 595f5f5f 4c455f5f 4c455f5f 544c4552 455f5f5f
  //   4c455f5f 45445f5f 595f5f5f 45424152 4f4e5f5f 455f5f5f 525f5f5f 595f5f5f 455f5f5f 53485f5f 595f5f5f
  //   4c455f5f 4c49455f 43455f5f 4e434544 5f5f5f5f 4c495348 5f5f5f5f 525f5f5f 42414c4c 5f5f5f5f 5f5f5f5f
  //   5f5f5f5f 4d414e5f 455f5f5f 5f5f5f5f 4152425f 475f5f5f 455f5f5f 544f505f 524f4f54 455f5f5f 414c5f5f
  //   5445445f 52595f5f 4e595f5f 455f5f5f 455f5f5f 4f545f5f 4b595f5f 5f5f5f5f 455f5f5f 524f4f4d 54424f5f
  //   485f5f5f 53545f5f 4e5f5f5f 4f585f5f 45484f47 43545f5f 47455f5f 455f5f5f 455f5f5f 4c455f5f 554d415f
  //   524f4f4d 5f5f5f5f 4c455f5f 485f5f5f 545f5f5f 545f5f5f 455f5f5f 5f5f5f5f 575f5f5f 53544943 455f5f5f
  //   53485f5f 41524d5f 494c455f 4c455f5f 535f5f5f 41544943 5f5f5f5f 5f5f5f5f 535f5f5f 415f5f5f 4c5f5f5f
  //   455f5f5f 5f5f5f5f 4748545f 545f5f5f 545f5f5f 4e415f5f 5f5f5f5f 5f5f5f5f 5f5f5f5f 4e49505f 485f5f5f
  //   4c495345 505f5f5f 455f5f5f 4c5f5f5f 45445f5f 505f5f5f 4f4e5f5f 45525f5f 455f5f5f 505f5f5f 4e5f5f5f
  //   52595f5f 4944455f 4c455f5f 535f5f5f 4e454c5f 415f5f5f 4c455f5f 445f5f5f 454c5f5f 455f5f5f 5f5f5f5f
  //   44595f5f 45525f5f 4945535f 5f5f5f5f 55414c5f 55535f5f 485f5f5f 5f5f5f5f 5349535f 41544552 5f5f5f5f
  //   5f5f5f5f 455f5f5f 48414e54 4c455f5f 5f5f5f5f 525f5f5f 545f5f5f 545f5f5f 5f5f5f5f 4c5f5f5f 52454c5f
  //   5f5f5f5f 49505f5f 5f5f5f5f 575f5f5f 4c415445 4f4f4e5f 4e5f5f5f 49474854 414c5f5f 5f5f5f5f 48455f5f
  //   49545f5f 43455f5f 43485f5f 54494f4e 4f575f5f 4c455f5f 485f5f5f 5445525f 4947414e 5f5f5f5f 43485f5f
  //   5f5f5f5f 4c5f5f5f 5449435f 485f5f5f 454e545f 56415445 43545f5f 5f5f5f5f 54554d5f 4445525f 4748545f
  //   5449435f 4b5f5f5f 4e545f5f 47485f5f 4c5f5f5f 4553545f 5445525f 455f5f5f 455f5f5f 4f4d5f5f 41525f5f
  //   455f5f5f 4147455f 53544f52 45525f5f 45445f5f 5f5f5f5f 45525f5f 45545f5f 455f5f5f 45535f5f 57414c4b
  //   435f5f5f 4c455f5f 54535f5f 5253455f 4c455f5f 49435f5f 55535f5f 4e47455f 45535345 4c54485f 41474553
  //   484d5f5f 52414c5f 4c5f5f5f 5049545f 484d4943 455f5f5f 4c5f5f5f 48414c4c 54544f5f 545f5f5f 504c455f
  //   455f5f5f 574f4f44 5445445f 504c455f 43455f5f 455f5f5f 52414c5f 545f5f5f 55455f5f 52595f5f 47595f5f
  //   455f5f5f 455f5f5f 55545f5f 4646455f 455f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
  //   contents of rom_2 (hex, n*v repeats v):
  //   53544f41 42554447 5a454252 50454e47 42454143 42554447 5a49475a 4c494f4e 42454144 43554447 594f594f
  //   4c494f4e 42454c49 434c4f55 594f4755 4348494d 42494f50 414c4f55 59554d4d 50415252 424c4143 464c4f4f
  //   444f4f4c 524f4249 424c4144 464f4f54 5a494e4e 53504152 424c414e 42415345 5a4f4f4c 53544152 424c4541
  //   42415349 5a455354 43484943 424c5545 4c4f4f50 59454c4c 464f585f 424c5545 504c4149 594f4445 50494e47
  //   42554646 504c4541 594f4741 50454e4e 43414447 474c5554 58524159 4e494748 43484154 554c554c 57484954
  //   4e494748 43484541 484f5345 5749434b 4c41524b 43484545 54484553 57414c4c 4b455942 43484950 45494748
  //   57415242 4b454e4e 434c4153 46494645 57454c4c 4b495445 434c4f53 48454c4c 56455353 4b495443 434c4f53
  //   50494c4c 56414355 4b4e4954 434c4f53 4841545f 56414341 4b4e4954 434c4f54 434f4154 56414c56 4b554d51
  //   434f434f 424f4f54 56494e54 4b455454 434f4646 53484f45 56414e49 4b495445 434f4c4c 414e474c 56454e44
  //   4e454544 434f4e53 53484946 56454e4f 50494e5f 44414242 424c4f55 56494c4c 53455749 44414646 4c454144
  //   56494e45 43524f43 44454146 4341545f 56495249 43524f53 4445434f 444f475f 57494c4c 4e4f5547 44454645
  //   5049475f 57484954 48414e47 44454645 43484154 57454444 48414e47 4445464c 504c4541 57494e44 484f4e45
  //   4445464c 4f50504f 57494e54 48594d4e 44454c49 50415041 57495245 53545249 44455350 504c4154 57495245
  //   53545249 44494745 53504f4f 57495443 5354524f 45445543 434c5542 57495a41 49524f4e 45464645 42554c4c
  //   5741524c 5a494e43 46414255 50414c4c 57495344 43415242 46415354 50494c41 574f4c46 4e414d45 46454c54
  //   454c465f 574f4d42 4e494748 46455454 53454c46 574f4f44 50594a41 46455544 5348454c 574f4f4c 5357494d
  //   46494c43 5348454c 57494c44 44414e43 46494c4c 4c4f4c4c 554e4956 534b4950 464c4154 4c4f4c4c 554d4252
  //   53434953 464c4553 4c4f4c4c 55534546 4b4e4956 464c4945 504f4c4c 554e4953 464f524b 464c4947 504f505f
  //   554e5350 53504f4f 464c4950 53495341 56494f4c 54454e53 464c4f41 4c415353 56494f4c 5354414e 464c4f55
  //   48415353 57414e44 434f4d46 464f4953 48555354 57484953 5350494b 46555449 42555354 57484953 53504143
  //   47414242 50495050 5741434b 53504143 47414c4c 50495354 4e455645 4d554444 47454553 504f4c49 43414e44
  //   50554444 4748494c 504f4c49 54524f55 534e4f57 47484f55 54494c54 52495645 534e4f57 47494c4c 42495445
  //   5245445f 534e4f57 474c4144 54485547 52485542 534c494e 474c4944 50495453 42454554 534c494d 474c4f42
  //   5354494c 43454c45 534b494e 474f4f53 414e4f44 43415252 4348414c 4845414c 44494f44 4d555348 5041494e
  //   48454154 44455349 4c454d4f 544f5942 48454447 44454645 4f52414e 53544f52 48454447 42414242 53415453
  //   52455354 4845454c 42554242 50454143 57524953 484f4953 4741424c 504c554d 454c424f 484f4c49 5341424c
  //   52414449 464f5245 484f5354 53544142 4245414e 4452414d 48554745 434f4f50 42454152 4452414d 49444541
  //   53434f50 50454152 44454c49 4944494f 53434f4f 42414e41 4d41524b 49534c45 53504f54 50415253 4d415243
  //   4c4f4341 53434f4f 4d415556 41505249 4c4f4f50 534c4f4f 4d41524f 53484f57 4c4f4f53 53544f4f 47524545
  //   4d454d4f 4f555453 544f5050 47524153 464c414e 50415354 54495050 4752414e 46454e4e 50415354 50495045
  //   5452454e 434f524e 50415354 474f4f44 56495254 46554e47 50454143 4241445f 4e454d45 414e5445 5045454c
  //   464c4950 4e455256 454c4550 50454f50 464c4f50 46454d55 4749414e 50494c4f 47494654 534b554c 57415354
  //   50494e5f 46494c4c 4b494e47 53545241 504f5055 53504954 51554545 53545241 504f5354 5055425f 51554943
  //   53545241 504f4c49 424c4541 51554553 4e415252 50554444 50495443 51554152 43415244 53414c45 474c4954
  //   48414c46 45584345 53434550 42495443 504f5254 455f4341 53454c45 49544348 5155414e 4255494c 534c4549
  //   504c4153 51554152 43454d45 534c4549 4348494c 52455155 504c4153 53504143 534c4f50 52414e44 4d4f5254
  //   53504144 43414242 52455349 524f4f46 53504943 48454c50 504c4558 43415250 53504943 534c4f50 524f5045
  //   50414e49 53544150 4c494748 52455645 4e494242 53544154 41424143 52455645 4e4f424c 53544541 53415553
  //   52485954 4e415455 53544541 464c4541 52485954 474e4f4d 53544545 504f4f4c 5249534f 4741554e 53544545
  //   504c4143 524f5345 4752414e 53544950 504c4149 4d41504c 47454e45 53544f41 504c4147 43484552 4752554e
  //   53544f4c 4150504c 57414c4e 47495241 5354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
endmodule

module Letter_Display_Driver (
  input  [6:0] ASCII_code_in,
  output [6:0] Col_0_out,
  output [6:0] Col_1_out,
  output [6:0] Col_2_out,
  output [6:0] Col_3_out,
  output [6:0] Col_4_out
);

  wire [4:0] multiplexer_1_out;
  wire [4:4] and_1_out;

  Multiplexer #(.width(5), .disabled(0), .enable("false")) multiplexer_1 (
    .in0({5{and_1_out[4]}}), .in1(ASCII_code_in[4:0]), .out(multiplexer_1_out), .sel(and_1_out[4]));
  and and_1 (and_1_out[4], ~ASCII_code_in[5], ASCII_code_in[6]);  // AND_Gate
  ROM #(.addrWidth(5), .dataWidth(7)) rom_1 (.addr(multiplexer_1_out), .data(Col_0_out));  // open: sel
  ROM #(.addrWidth(5), .dataWidth(7)) rom_2 (.addr(multiplexer_1_out), .data(Col_1_out));  // open: sel
  ROM #(.addrWidth(5), .dataWidth(7)) rom_3 (.addr(multiplexer_1_out), .data(Col_2_out));  // open: sel
  ROM #(.addrWidth(5), .dataWidth(7)) rom_4 (.addr(multiplexer_1_out), .data(Col_3_out));  // open: sel
  ROM #(.addrWidth(5), .dataWidth(7)) rom_5 (.addr(multiplexer_1_out), .data(Col_4_out));  // open: sel
  // Probe on ASCII_code_in

  // Notes on the sheet:
  //   contents of rom_1 (hex, n*v repeats v):
  //   0 3f 7f 3e 7f 7f 7f 3e 7f 0 42 4*7f 3e 7f 3e 7f 32 40 7e 7c 7f 63 60 43 4*0 8
  //   contents of rom_2 (hex, n*v repeats v):
  //   0 48 49 41 41 49 48 41 8 41 41 8 1 20 30 41 48 41 48 49 40 1 6 6 36 18 47 4*0 8
  //   contents of rom_3 (hex, n*v repeats v):
  //   0 48 49 41 41 49 48 41 8 7f 7e 14 1 10 1c 41 48 41 48 49 7f 1 3 c 1c f 4d 4*0 8
  //   contents of rom_4 (hex, n*v repeats v):
  //   0 48 49 41 41 49 48 45 8 41 40 22 1 20 6 41 48 3f 4c 49 40 1 6 6 36 18 59 4*0 8
  //   contents of rom_5 (hex, n*v repeats v):
  //   0 3f 36 41 3e 49 48 26 7f 0 40 41 1 7f 7f 3e 30 1 33 26 40 7e 7c 7f 63 60 71 4*0 8
  //   Drives a 5 column 7 row LED. Letters A_Z and "-" are displayed when corresponding ASCII code is input
endmodule

module Blank_or_Letter (
  input  [6:0] Letter_Guessed,
  input  New_Game,
  input  Button_Pressed,
  output [6:0] Letter_Code
);

  wire [6:0] multiplexer_1_out;

  Multiplexer #(.width(7), .enable("false")) multiplexer_1 (
    .in0(Letter_Guessed), .in1(7'b1011111), .out(multiplexer_1_out), .sel(New_Game));
  Register #(.width(7)) register_1 (.D(multiplexer_1_out), .Q(Letter_Code), .clk(Button_Pressed));  // open: en, clr
endmodule

module Letter_Matcher (
  input  [6:0] Letter_code,
  input  [6:0] Letter_from_word,
  output Match
);

  wire [6:0] xnor_1_out;

  assign xnor_1_out = ~(Letter_code ^ Letter_from_word);  // XNOR_Gate xnor_1, 7 bits wide
  and and_1 (Match, xnor_1_out[0], xnor_1_out[1], xnor_1_out[2], xnor_1_out[3], xnor_1_out[4], xnor_1_out[5], xnor_1_out[6]);
endmodule

module Find_Matches (
  input  [6:0] Letter_code,
  input  [6:0] Letter_0,
  input  [6:0] Letter_1,
  input  [6:0] Letter_2,
  input  [6:0] Letter_3,
  input  [6:0] Letter_4,
  input  [6:0] Letter_5,
  input  [6:0] Letter_6,
  input  [6:0] Letter_7,
  output [7:0] Matches,
  output any_matches
);

  Letter_Matcher letter_matcher_1 (.Letter_code(Letter_code), .Letter_from_word(Letter_0), .Match(Matches[7]));
  Letter_Matcher letter_matcher_2 (.Letter_code(Letter_code), .Letter_from_word(Letter_1), .Match(Matches[6]));
  Letter_Matcher letter_matcher_3 (.Letter_code(Letter_code), .Letter_from_word(Letter_2), .Match(Matches[5]));
  Letter_Matcher letter_matcher_4 (.Letter_code(Letter_code), .Letter_from_word(Letter_3), .Match(Matches[4]));
  Letter_Matcher letter_matcher_5 (.Letter_code(Letter_code), .Letter_from_word(Letter_4), .Match(Matches[3]));
  Letter_Matcher letter_matcher_6 (.Letter_code(Letter_code), .Letter_from_word(Letter_5), .Match(Matches[2]));
  Letter_Matcher letter_matcher_7 (.Letter_code(Letter_code), .Letter_from_word(Letter_6), .Match(Matches[1]));
  Letter_Matcher letter_matcher_8 (.Letter_code(Letter_code), .Letter_from_word(Letter_7), .Match(Matches[0]));
  or or_1 (any_matches, Matches[7], Matches[6], Matches[5], Matches[4], Matches[3], Matches[2], Matches[1], Matches[0]);
endmodule

module gallows (
  input  [3:0] bus_0,
  output [15:0] Col_0_out,
  output [15:0] Col_1_out,
  output [15:0] Col_2_out,
  output [15:0] Col_3_out,
  output [15:0] Col_4_out,
  output [15:0] Col_0_out_2,
  output [15:0] Col_1_out_2,
  output [15:0] Col_2_out_2,
  output [15:0] Col_3_out_2,
  output [15:0] Col_4_out_2,
  output [15:0] Col_0_out_3,
  output [15:0] Col_1_out_3,
  output [15:0] Col_2_out_3,
  output [15:0] Col_3_out_3
);

  // Probe on bus_0
  ROM #(.addrWidth(4), .dataWidth(16)) rom_1 (.addr(bus_0), .data(Col_0_out));  // open: sel
  ROM #(.addrWidth(4), .dataWidth(16)) rom_2 (.addr(bus_0), .data(Col_1_out));  // open: sel
  ROM #(.addrWidth(4), .dataWidth(16)) rom_3 (.addr(bus_0), .data(Col_2_out));  // open: sel
  ROM #(.addrWidth(4), .dataWidth(16)) rom_4 (.addr(bus_0), .data(Col_3_out));  // open: sel
  ROM #(.addrWidth(4), .dataWidth(16)) rom_5 (.addr(bus_0), .data(Col_4_out));  // open: sel
  ROM #(.addrWidth(4), .dataWidth(16)) rom_6 (.addr(bus_0), .data(Col_0_out_2));  // open: sel
  ROM #(.addrWidth(4), .dataWidth(16)) rom_7 (.addr(bus_0), .data(Col_1_out_2));  // open: sel
  ROM #(.addrWidth(4), .dataWidth(16)) rom_8 (.addr(bus_0), .data(Col_2_out_2));  // open: sel
  ROM #(.addrWidth(4), .dataWidth(16)) rom_9 (.addr(bus_0), .data(Col_3_out_2));  // open: sel
  ROM #(.addrWidth(4), .dataWidth(16)) rom_10 (.addr(bus_0), .data(Col_4_out_2));  // open: sel
  ROM #(.addrWidth(4), .dataWidth(16)) rom_11 (.addr(bus_0), .data(Col_0_out_3));  // open: sel
  ROM #(.addrWidth(4), .dataWidth(16)) rom_12 (.addr(bus_0), .data(Col_1_out_3));  // open: sel
  ROM #(.addrWidth(4), .dataWidth(16)) rom_13 (.addr(bus_0), .data(Col_2_out_3));  // open: sel
  ROM #(.addrWidth(4), .dataWidth(16)) rom_14 (.addr(bus_0), .data(Col_3_out_3));  // open: sel

  // Notes on the sheet:
  //   room1
  //   room2
  //   room3
  //   room4
  //   room5
  //   contents of rom_1 (hex, n*v repeats v):
  //   0 11*1 4*6006
  //   contents of rom_2 (hex, n*v repeats v):
  //   0 1 10*ffff 4*6006
  //   contents of rom_3 (hex, n*v repeats v):
  //   0 1 1 8001 8*8801 4*1818
  //   contents of rom_4 (hex, n*v repeats v):
  //   0 1 1 8001 8*9001 4*1818
  //   contents of rom_5 (hex, n*v repeats v):
  //   0 1 1 8001 8*a001 4*660
  //   room6
  //   room7
  //   room8
  //   room9
  //   room10
  //   contents of rom_6 (hex, n*v repeats v):
  //   0 0 0 8000 6*c000 c002 c002 4*660
  //   contents of rom_7 (hex, n*v repeats v):
  //   0 0 0 5*8000 8100 8100 8104 8104 4*180
  //   contents of rom_8 (hex, n*v repeats v):
  //   0 0 0 5*8000 8100 8100 8108 8108 4*180
  //   contents of rom_9 (hex, n*v repeats v):
  //   0 0 0 8000 8000 8000 9c00 9c00 9d00 9d00 9d10 9d10 4*660
  //   contents of rom_10 (hex, n*v repeats v):
  //   0 0 0 8000 8000 e000 f400 5*f7e0 4*660
  //   contents of rom_11 (hex, n*v repeats v):
  //   0 0 0 8000 8000 8000 9c00 9c00 9c00 9d00 9d00 9d10 4*1818
  //   room11
  //   contents of rom_12 (hex, n*v repeats v):
  //   9*0 100 100 108 4*1818
  //   room12
  //   contents of rom_13 (hex, n*v repeats v):
  //   9*0 100 100 104 4*6006
  //   room13
  //   contents of rom_14 (hex, n*v repeats v):
  //   11*0 2 4*6006
  //   room14
endmodule

module words (
  input  [8:0] _9_bit_address
);

  ROM #(.addrWidth(9), .dataWidth(32)) rom_1 (.addr(_9_bit_address));  // open: data, sel
  ROM #(.addrWidth(9), .dataWidth(32)) rom_2 (.addr(_9_bit_address));  // open: data, sel

  // Notes on the sheet:
  //   contents of rom_1 (hex, n*v repeats v):
  //   545f5f5f 49455f5f 415f5f5f 55494e5f 485f5f5f 455f5f5f 41475f5f 5f5f5f5f 45445f5f 454c5f5f 5f5f5f5f
  //   4553535f 45465f5f 445f5f5f 52545f5f 505f5f5f 49435f5f 445f5f5f 595f5f5f 4f545f5f 4b5f5f5f 4445445f
  //   414c4c59 4e5f5f5f 455f5f5f 49455f5f 49415f5f 524f575f 445f5f5f 42414c4c 4f47595f 4c494e47 545f5f5f
  //   435f5f5f 5f5f5f5f 4b454e5f 42454c4c 484f4c45 4f575f5f 5f5f5f5f 5f5f5f5f 5445445f 4c5f5f5f 504f4e47
  //   45545f5f 5445445f 5f5f5f5f 595f5f5f 455f5f5f 45414c5f 5f5f5f5f 545f5f5f 544c455f 4154455f 455f5f5f
  //   544f574c 545f5f5f 5f5f5f5f 45525f5f 5f5f5f5f 53455f5f 455f5f5f 4f575f5f 4f415244 5f5f5f5f 545f5f5f
  //   4c45525f 454c5f5f 5349435f 5f5f5f5f 49455f5f 5f5f5f5f 4553545f 4f5f5f5f 454c5f5f 48454e5f 45545f5f
  //   5f5f5f5f 554d5f5f 5f5f5f5f 455f5f5f 5f5f5f5f 4e43595f 54494e47 4845535f 5f5f5f5f 455f5f5f 5541545f
  //   415f5f5f 5f5f5f5f 4147455f 4c455f5f 45455f5f 5f5f5f5f 53485f5f 53555246 4154455f 455f5f5f 45545441
  //   4c455f5f 54414e54 545f5f5f 4d5f5f5f 5f5f5f5f 4c455f5f 53455f5f 41494e5f 4e475f5f 4f44494c 5f5f5f5f
  //   4741525f 4845545f 5f5f5f5f 5f5f5f5f 4449414e 535f5f5f 44455f5f 5f5f5f5f 4f575f5f 48545f5f 41545f5f
  //   5f5f5f5f 455f5f5f 4d414e5f 43545f5f 5f5f5f5f 494e475f 45525f5f 4154455f 53455f5f 4f575f5f 5354595f
  //   4543545f 53455f5f 45525f5f 5f5f5f5f 4748545f 4c5f5f5f 5f5f5f5f 4e475f5f 4954455f 455f5f5f 4c455353
  //   4e47595f 53545f5f 465f5f5f 485f5f5f 4e475f5f 4154455f 5f5f5f5f 52445f5f 5f5f5f5f 43545f5f 4953485f
  //   4f434b5f 5f5f5f5f 4c4f5553 49415445 4f4d5f5f 4f4e5f5f 5f5f5f5f 5445535f 5f5f5f5f 4c455353 5f5f5f5f
  //   5f5f5f5f 4c455f5f 54434150 4c455f5f 5f5f5f5f 454e5f5f 4d41535f 414c5f5f 465f5f5f 4c454e5f 4d494e47
  //   485f5f5f 4c5f5f5f 574f4f44 494e475f 45545f5f 4f505f5f 45525345 50494e47 5f5f5f5f 49504f50 454c4c41
  //   534f5253 485f5f5f 5f5f5f5f 554c5f5f 45535f5f 535f5f5f 5f5f5f5f 4f4e5f5f 535f5f5f 48545f5f 5f5f5f5f
  //   4f494c54 4e535f5f 464c4f50 4c5f5f5f 45545f5f 455f5f5f 545f5f5f 5f5f5f5f 454e545f 44415244 545f5f5f
  //   4c455f5f 45524552 4f52545f 545f5f5f 4c455f5f 544c455f 595f5f5f 4c455f5f 4c455f5f 544c4552 455f5f5f
  //   4c455f5f 45445f5f 595f5f5f 45424152 4f4e5f5f 455f5f5f 525f5f5f 595f5f5f 455f5f5f 53485f5f 595f5f5f
  //   4c455f5f 4c49455f 43455f5f 4e434544 5f5f5f5f 4c495348 5f5f5f5f 525f5f5f 42414c4c 5f5f5f5f 5f5f5f5f
  //   5f5f5f5f 4d414e5f 455f5f5f 5f5f5f5f 4152425f 475f5f5f 455f5f5f 544f505f 524f4f54 455f5f5f 414c5f5f
  //   5445445f 52595f5f 4e595f5f 455f5f5f 455f5f5f 4f545f5f 4b595f5f 5f5f5f5f 455f5f5f 524f4f4d 54424f5f
  //   485f5f5f 53545f5f 4e5f5f5f 4f585f5f 45484f47 43545f5f 47455f5f 455f5f5f 455f5f5f 4c455f5f 554d415f
  //   524f4f4d 5f5f5f5f 4c455f5f 485f5f5f 545f5f5f 545f5f5f 455f5f5f 5f5f5f5f 575f5f5f 53544943 455f5f5f
  //   53485f5f 41524d5f 494c455f 4c455f5f 535f5f5f 41544943 5f5f5f5f 5f5f5f5f 535f5f5f 415f5f5f 4c5f5f5f
  //   455f5f5f 5f5f5f5f 4748545f 545f5f5f 545f5f5f 4e415f5f 5f5f5f5f 5f5f5f5f 5f5f5f5f 4e49505f 485f5f5f
  //   4c495345 505f5f5f 455f5f5f 4c5f5f5f 45445f5f 505f5f5f 4f4e5f5f 45525f5f 455f5f5f 505f5f5f 4e5f5f5f
  //   52595f5f 4944455f 4c455f5f 535f5f5f 4e454c5f 415f5f5f 4c455f5f 445f5f5f 454c5f5f 455f5f5f 5f5f5f5f
  //   44595f5f 45525f5f 4945535f 5f5f5f5f 55414c5f 55535f5f 485f5f5f 5f5f5f5f 5349535f 41544552 5f5f5f5f
  //   5f5f5f5f 455f5f5f 48414e54 4c455f5f 5f5f5f5f 525f5f5f 545f5f5f 545f5f5f 5f5f5f5f 4c5f5f5f 52454c5f
  //   5f5f5f5f 49505f5f 5f5f5f5f 575f5f5f 4c415445 4f4f4e5f 4e5f5f5f 49474854 414c5f5f 5f5f5f5f 48455f5f
  //   49545f5f 43455f5f 43485f5f 54494f4e 4f575f5f 4c455f5f 485f5f5f 5445525f 4947414e 5f5f5f5f 43485f5f
  //   5f5f5f5f 4c5f5f5f 5449435f 485f5f5f 454e545f 56415445 43545f5f 5f5f5f5f 54554d5f 4445525f 4748545f
  //   5449435f 4b5f5f5f 4e545f5f 47485f5f 4c5f5f5f 4553545f 5445525f 455f5f5f 455f5f5f 4f4d5f5f 41525f5f
  //   455f5f5f 4147455f 53544f52 45525f5f 45445f5f 5f5f5f5f 45525f5f 45545f5f 455f5f5f 45535f5f 57414c4b
  //   435f5f5f 4c455f5f 54535f5f 5253455f 4c455f5f 49435f5f 55535f5f 4e47455f 45535345 4c54485f 41474553
  //   484d5f5f 52414c5f 4c5f5f5f 5049545f 484d4943 455f5f5f 4c5f5f5f 48414c4c 54544f5f 545f5f5f 504c455f
  //   455f5f5f 574f4f44 5445445f 504c455f 43455f5f 455f5f5f 52414c5f 545f5f5f 55455f5f 52595f5f 47595f5f
  //   455f5f5f 455f5f5f 55545f5f 4646455f 455f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
  //   contents of rom_2 (hex, n*v repeats v):
  //   53544f41 42554447 5a454252 50454e47 42454143 42554447 5a49475a 4c494f4e 42454144 43554447 594f594f
  //   4c494f4e 42454c49 434c4f55 594f4755 4348494d 42494f50 414c4f55 59554d4d 50415252 424c4143 464c4f4f
  //   444f4f4c 524f4249 424c4144 464f4f54 5a494e4e 53504152 424c414e 42415345 5a4f4f4c 53544152 424c4541
  //   42415349 5a455354 43484943 424c5545 4c4f4f50 59454c4c 464f585f 424c5545 504c4149 594f4445 50494e47
  //   42554646 504c4541 594f4741 50454e4e 43414447 474c5554 58524159 4e494748 43484154 554c554c 57484954
  //   4e494748 43484541 484f5345 5749434b 4c41524b 43484545 54484553 57414c4c 4b455942 43484950 45494748
  //   57415242 4b454e4e 434c4153 46494645 57454c4c 4b495445 434c4f53 48454c4c 56455353 4b495443 434c4f53
  //   50494c4c 56414355 4b4e4954 434c4f53 4841545f 56414341 4b4e4954 434c4f54 434f4154 56414c56 4b554d51
  //   434f434f 424f4f54 56494e54 4b455454 434f4646 53484f45 56414e49 4b495445 434f4c4c 414e474c 56454e44
  //   4e454544 434f4e53 53484946 56454e4f 50494e5f 44414242 424c4f55 56494c4c 53455749 44414646 4c454144
  //   56494e45 43524f43 44454146 4341545f 56495249 43524f53 4445434f 444f475f 57494c4c 4e4f5547 44454645
  //   5049475f 57484954 48414e47 44454645 43484154 57454444 48414e47 4445464c 504c4541 57494e44 484f4e45
  //   4445464c 4f50504f 57494e54 48594d4e 44454c49 50415041 57495245 53545249 44455350 504c4154 57495245
  //   53545249 44494745 53504f4f 57495443 5354524f 45445543 434c5542 57495a41 49524f4e 45464645 42554c4c
  //   5741524c 5a494e43 46414255 50414c4c 57495344 43415242 46415354 50494c41 574f4c46 4e414d45 46454c54
  //   454c465f 574f4d42 4e494748 46455454 53454c46 574f4f44 50594a41 46455544 5348454c 574f4f4c 5357494d
  //   46494c43 5348454c 57494c44 44414e43 46494c4c 4c4f4c4c 554e4956 534b4950 464c4154 4c4f4c4c 554d4252
  //   53434953 464c4553 4c4f4c4c 55534546 4b4e4956 464c4945 504f4c4c 554e4953 464f524b 464c4947 504f505f
  //   554e5350 53504f4f 464c4950 53495341 56494f4c 54454e53 464c4f41 4c415353 56494f4c 5354414e 464c4f55
  //   48415353 57414e44 434f4d46 464f4953 48555354 57484953 5350494b 46555449 42555354 57484953 53504143
  //   47414242 50495050 5741434b 53504143 47414c4c 50495354 4e455645 4d554444 47454553 504f4c49 43414e44
  //   50554444 4748494c 504f4c49 54524f55 534e4f57 47484f55 54494c54 52495645 534e4f57 47494c4c 42495445
  //   5245445f 534e4f57 474c4144 54485547 52485542 534c494e 474c4944 50495453 42454554 534c494d 474c4f42
  //   5354494c 43454c45 534b494e 474f4f53 414e4f44 43415252 4348414c 4845414c 44494f44 4d555348 5041494e
  //   48454154 44455349 4c454d4f 544f5942 48454447 44454645 4f52414e 53544f52 48454447 42414242 53415453
  //   52455354 4845454c 42554242 50454143 57524953 484f4953 4741424c 504c554d 454c424f 484f4c49 5341424c
  //   52414449 464f5245 484f5354 53544142 4245414e 4452414d 48554745 434f4f50 42454152 4452414d 49444541
  //   53434f50 50454152 44454c49 4944494f 534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
  //   letters 0-3
  //   letters 4-7
endmodule

module Light (
  input  letter_button,
  input  end_game,
  input  [6:0] ASCII,
  output light,
  output \wire ,
  output [6:0] latest_letter
);

  wire not_1_out, not_2_out, pull_resistor_1_node;
  wire [6:0] Register_q;

  Pull_Resistor #(.pull(1)) pull_resistor_1 (.node(pull_resistor_1_node));
  Transistor #(.\type ("n")) transistor_1 (.in(1'b0), .out(pull_resistor_1_node), .gate(letter_button));
  not not_1 (not_1_out, pull_resistor_1_node);
  not not_2 (not_2_out, not_1_out);
  Register #(.width(7), .trigger("falling")) Register (.D(ASCII), .Q(Register_q), .clk(not_2_out));  // open: en, clr
  S_R_Flip_Flop s_r_ff_1 (.Q(light), .preset(letter_button), .reset(end_game));  // open: S, clk, R, Qn, en
  assign latest_letter = letter_button ? Register_q : 7'bz;  // Controlled_Buffer controlled_buffer_1
  Multiplexer #(.enable("false")) multiplexer_1 (.in1(letter_button), .out(\wire ), .sel(letter_button));  // open: in0
endmodule

module correct_pattern (
  input  [7:0] \matches ,
  input  new_game,
  input  end_game,
  input  button_pressed,
  output [7:0] correct_pattern
);

  wire not_1_out, not_2_out, not_3_out, not_4_out, not_5_out, not_6_out, not_7_out, not_8_out, not_9_out,
       not_10_out, or_1_out, or_2_out;
  wire [7:0] multiplexer_1_out, register_1_q;

  Multiplexer #(.width(8), .enable("false")) multiplexer_1 (
    .in0(\matches ), .in1({8{1'b0}}), .out(multiplexer_1_out), .sel(end_game));
  not not_1 (not_1_out, not_2_out);
  not not_2 (not_2_out, or_1_out);
  or or_1 (or_1_out, end_game, button_pressed);
  not not_3 (not_3_out, register_1_q[0]);
  Register #(.width(1)) register_1 (
    .D(multiplexer_1_out[0]), .en(not_3_out), .Q(register_1_q[0]), .clk(not_1_out), .clr(or_2_out));
  not not_4 (not_4_out, register_1_q[1]);
  Register #(.width(1)) register_2 (
    .D(multiplexer_1_out[1]), .en(not_4_out), .Q(register_1_q[1]), .clk(not_1_out), .clr(or_2_out));
  Register #(.width(1)) register_3 (
    .D(multiplexer_1_out[2]), .en(not_5_out), .Q(register_1_q[2]), .clk(not_1_out), .clr(or_2_out));
  not not_5 (not_5_out, register_1_q[2]);
  Register #(.width(1)) register_4 (
    .D(multiplexer_1_out[3]), .en(not_6_out), .Q(register_1_q[3]), .clk(not_1_out), .clr(or_2_out));
  not not_6 (not_6_out, register_1_q[3]);
  Register #(.width(1)) register_5 (
    .D(multiplexer_1_out[4]), .en(not_7_out), .Q(register_1_q[4]), .clk(not_1_out), .clr(or_2_out));
  not not_7 (not_7_out, register_1_q[4]);
  not not_8 (not_8_out, register_1_q[5]);
  Register #(.width(1)) register_6 (
    .D(multiplexer_1_out[5]), .en(not_8_out), .Q(register_1_q[5]), .clk(not_1_out), .clr(or_2_out));
  Register #(.width(1)) register_7 (
    .D(multiplexer_1_out[6]), .en(not_9_out), .Q(register_1_q[6]), .clk(not_1_out), .clr(or_2_out));
  not not_9 (not_9_out, register_1_q[6]);
  not not_10 (not_10_out, register_1_q[7]);
  Register #(.width(1)) register_8 (
    .D(multiplexer_1_out[7]), .en(not_10_out), .Q(register_1_q[7]), .clk(not_1_out), .clr(or_2_out));
  or or_2 (or_2_out, new_game, end_game);
  Adder adder_1 (.a(register_1_q), .b({8{1'b0}}), .out(correct_pattern));  // open: cin, cout
endmodule

module wrong_guesses (
  input  new_game,
  input  end_game,
  input  button_pressed,
  input  any_matches,
  output [3:0] wrong_guesses
);

  wire and_1_out, comparator_1_eq, not_1_out, not_2_out, not_3_out, not_4_out, or_1_out, or_2_out;
  wire [3:0] adder_1_out, multiplexer_1_out;

  Adder #(.width(4)) adder_1 (.a(wrong_guesses), .b(4'b0001), .out(adder_1_out));  // open: cin, cout
  Multiplexer #(.width(4), .enable("false")) multiplexer_1 (
    .in0(adder_1_out), .in1(4'b0000), .out(multiplexer_1_out), .sel(end_game));
  // Probe on wrong_guesses
  Comparator #(.width(4), .mode("unsigned")) comparator_1 (
    .a(wrong_guesses), .b(4'b1100), .eq(comparator_1_eq));  // open: gt, lt
  not not_1 (not_1_out, comparator_1_eq);
  and and_1 (and_1_out, not_1_out, not_2_out);
  not not_2 (not_2_out, any_matches);
  not not_3 (not_3_out, not_4_out);
  not not_4 (not_4_out, or_1_out);
  or or_1 (or_1_out, end_game, button_pressed);
  Register #(.width(4)) register_1 (
    .D(multiplexer_1_out), .en(and_1_out), .Q(wrong_guesses), .clk(not_3_out), .clr(or_2_out));
  // AND_Gate and_2 has open pins: in0=wrong_guesses[0], in1=wrong_guesses[1], in2=wrong_guesses[2], in3=wrong_guesses[3], out=open
  or or_2 (or_2_out, new_game, end_game);
endmodule

module Display (
  input  [6:0] letter_code_7,
  input  [7:0] \matches ,
  input  button_pressed,
  input  end_game,
  input  new_game,
  output [6:0] ASCII_code_out,
  output [6:0] ASCII_code_out_2,
  output [6:0] ASCII_code_out_3,
  output [6:0] ASCII_code_out_4,
  output [6:0] ASCII_code_out_5,
  output [6:0] ASCII_code_out_6,
  output [6:0] ASCII_code_out_7,
  output [6:0] ASCII_code_out_8
);

  wire or_1_out, or_2_out;
  wire [6:0] multiplexer_1_out, multiplexer_2_out, multiplexer_3_out, multiplexer_4_out, multiplexer_6_out,
       multiplexer_7_out, multiplexer_8_out, multiplexer_9_out;
  wire [7:0] multiplexer_5_out;

  Multiplexer #(.width(7), .enable("false")) multiplexer_1 (
    .in0({7{1'b0}}), .in1(letter_code_7), .out(multiplexer_1_out), .sel(multiplexer_5_out[7]));
  Register #(.width(7), .trigger("high")) register_1 (
    .D(multiplexer_1_out), .en(multiplexer_5_out[7]), .Q(ASCII_code_out), .clk(or_1_out), .clr(or_2_out));
  Register #(.width(7), .trigger("high")) register_2 (
    .D(multiplexer_2_out), .en(multiplexer_5_out[6]), .Q(ASCII_code_out_2), .clk(or_1_out), .clr(or_2_out));
  Multiplexer #(.width(7), .enable("false")) multiplexer_2 (
    .in0({7{1'b0}}), .in1(letter_code_7), .out(multiplexer_2_out), .sel(multiplexer_5_out[6]));
  Multiplexer #(.width(7), .enable("false")) multiplexer_3 (
    .in0({7{1'b0}}), .in1(letter_code_7), .out(multiplexer_3_out), .sel(multiplexer_5_out[5]));
  Register #(.width(7), .trigger("high")) register_3 (
    .D(multiplexer_3_out), .en(multiplexer_5_out[5]), .Q(ASCII_code_out_3), .clk(or_1_out), .clr(or_2_out));
  Multiplexer #(.width(7), .enable("false")) multiplexer_4 (
    .in0({7{1'b0}}), .in1(letter_code_7), .out(multiplexer_4_out), .sel(multiplexer_5_out[4]));
  Register #(.width(7), .trigger("high")) register_4 (
    .D(multiplexer_4_out), .en(multiplexer_5_out[4]), .Q(ASCII_code_out_4), .clk(or_1_out), .clr(or_2_out));
  Multiplexer #(.width(8), .enable("false")) multiplexer_5 (
    .in0(\matches ), .in1({8{1'b1}}), .out(multiplexer_5_out), .sel(1'b0));
  Register #(.width(7), .trigger("high")) register_5 (
    .D(multiplexer_6_out), .en(multiplexer_5_out[3]), .Q(ASCII_code_out_5), .clk(or_1_out), .clr(or_2_out));
  Multiplexer #(.width(7), .enable("false")) multiplexer_6 (
    .in0({7{1'b0}}), .in1(letter_code_7), .out(multiplexer_6_out), .sel(multiplexer_5_out[3]));
  Register #(.width(7), .trigger("high")) register_6 (
    .D(multiplexer_7_out), .en(multiplexer_5_out[2]), .Q(ASCII_code_out_6), .clk(or_1_out), .clr(or_2_out));
  Multiplexer #(.width(7), .enable("false")) multiplexer_7 (
    .in0({7{1'b0}}), .in1(letter_code_7), .out(multiplexer_7_out), .sel(multiplexer_5_out[2]));
  Multiplexer #(.width(7), .enable("false")) multiplexer_8 (
    .in0({7{1'b0}}), .in1(letter_code_7), .out(multiplexer_8_out), .sel(multiplexer_5_out[1]));
  Register #(.width(7), .trigger("high")) register_7 (
    .D(multiplexer_8_out), .en(multiplexer_5_out[1]), .Q(ASCII_code_out_7), .clk(or_1_out), .clr(or_2_out));
  Multiplexer #(.width(7), .enable("false")) multiplexer_9 (
    .in0({7{1'b0}}), .in1(letter_code_7), .out(multiplexer_9_out), .sel(multiplexer_5_out[0]));
  Register #(.width(7), .trigger("high")) register_8 (
    .D(multiplexer_9_out), .en(multiplexer_5_out[0]), .Q(ASCII_code_out_8), .clk(or_1_out), .clr(or_2_out));
  or or_1 (or_1_out, button_pressed, end_game, new_game);
  or or_2 (or_2_out, end_game, new_game);
endmodule

module Light2 (
  input  letter_button,
  input  end_game,
  input  [6:0] ASCII,
  output light,
  output [6:0] latest_letter,
  output \wire 
);

  wire and_1_out, multiplexer_1_out, or_1_out;

  assign latest_letter = letter_button ? ASCII : 7'bz;  // Controlled_Buffer controlled_buffer_1
  Multiplexer #(.enable("false")) multiplexer_1 (
    .in0(letter_button), .in1(1'b0), .out(multiplexer_1_out), .sel(end_game));
  Register #(.width(1), .trigger("falling")) register_1 (
    .D(multiplexer_1_out), .Q(light), .clk(or_1_out));  // open: en, clr
  or or_1 (or_1_out, letter_button, end_game);
  and and_1 (and_1_out, ~light, letter_button);  // AND_Gate
  Transistor #(.\type ("n")) transistor_1 (.in(1'b0), .out(\wire ), .gate(and_1_out));
endmodule

module losses (
  input  end_game,
  input  [3:0] Wrong_guesses,
  output [3:0] losses
);

  wire comparator_1_eq;
  wire [3:0] adder_1_out;

  Adder #(.width(4)) adder_1 (.a(losses), .b(4'b0001), .out(adder_1_out));  // open: cin, cout
  Comparator #(.width(5)) comparator_1 (.a(5'b01100), .b({1'b0, Wrong_guesses}), .eq(comparator_1_eq));  // open: gt, lt
  Register #(.width(4)) register_1 (.D(adder_1_out), .Q(losses), .clk(comparator_1_eq), .clr(end_game));  // open: en
endmodule

module wins (
  input  [7:0] correct_pattern,
  input  end_game,
  output [3:0] Wins
);

  wire and_1_out;
  wire [3:0] adder_1_out;

  and and_1 (and_1_out, correct_pattern[0], correct_pattern[1], correct_pattern[2], correct_pattern[3], correct_pattern[4], correct_pattern[5], correct_pattern[6], correct_pattern[7]);
  Adder #(.width(4)) adder_1 (.a(Wins), .b(4'b0001), .out(adder_1_out));  // open: cin, cout
  Register #(.width(4)) register_1 (.D(adder_1_out), .Q(Wins), .clk(and_1_out), .clr(end_game));  // open: en
endmodule

module panel (
  input  in_1,
  input  in_2,
  input  in_3,
  input  in_4,
  input  in_5,
  input  in_6,
  input  in_7,
  input  in_8,
  input  in_9,
  input  in_10,
  input  in_11,
  input  in_12,
  input  in_13,
  input  in_14,
  input  in_15,
  input  in_16,
  input  in_17,
  input  in_18,
  input  in_19,
  input  in_20,
  input  in_21,
  input  in_22,
  input  in_23,
  input  in_24,
  input  in_25,
  input  in_26,
  input  [3:0] WRONG_GUESSES,
  input  stop,
  input  [7:0] Correct_pattern,
  input  [7:0] Matches,
  input  no_button,
  input  [6:0] TTY,
  input  tick_TTY,
  input  yes_button,
  input  LOSES,
  input  WIN,
  input  START_prime,
  output out_38,
  output out_39,
  output out_40,
  output out_41,
  output out_42,
  output out_43,
  output out_44,
  output out_45,
  output out_46,
  output out_47,
  output [15:0] out_48,
  output [15:0] out_49,
  output [15:0] out_50,
  output [15:0] out_51,
  output [15:0] out_52,
  output [15:0] out_53,
  output [15:0] out_54,
  output [15:0] out_55,
  output out_56,
  output out_57,
  output out_58,
  output out_59,
  output out_60,
  output [15:0] out_61,
  output [15:0] out_62,
  output [15:0] out_63,
  output [15:0] out_64,
  output [15:0] out_65,
  output [15:0] out_66,
  output out_67,
  output out_68,
  output out_69,
  output out_70,
  output out_71,
  output out_72,
  output out_73,
  output out_74,
  output out_75,
  output out_76,
  output out_77,
  output [3:0] out_78,
  output [3:0] out_79,
  output new_game,
  output [6:0] letter_code,
  output [6:0] out_82,
  output [6:0] out_83,
  output [6:0] out_84,
  output [6:0] out_85,
  output [6:0] out_86,
  output [6:0] out_87,
  output [6:0] out_88,
  output [6:0] out_89,
  output END_GAME,
  output buttoon_pressed,
  output [6:0] out_92,
  output out_93,
  output out_94,
  output YES,
  output NO
);

  wire light2_1_wire, not_1_out, not_3_out, or_1_out, xor_1_out, xor_2_out;
  wire [6:0] light2_1_latest_letter, multiplexer_1_out;

  Multiplexer #(.width(7), .enable("false")) multiplexer_1 (
    .in0(light2_1_latest_letter), .in1(7'b1011111), .out(multiplexer_1_out), .sel(new_game));
  not not_1 (not_1_out, stop);
  or or_1 (or_1_out, new_game, stop);
  Register #(.width(7), .trigger("low")) register_1 (
    .D(multiplexer_1_out), .en(not_1_out), .Q(letter_code), .clk(xor_1_out), .clr(END_GAME));
  xor xor_1 (xor_1_out, new_game, buttoon_pressed);
  Light2 light2_1 (
    .end_game(or_1_out), .ASCII(7'b1000001), .letter_button(in_1), .light(out_38),
    .latest_letter(light2_1_latest_letter), .\wire (light2_1_wire));
  Light2 light2_2 (
    .end_game(or_1_out), .ASCII(7'b1000110), .letter_button(in_6), .light(out_43),
    .latest_letter(light2_1_latest_letter), .\wire (light2_1_wire));
  Light2 light2_3 (
    .end_game(or_1_out), .ASCII(7'b1001011), .letter_button(in_11), .light(out_56),
    .latest_letter(light2_1_latest_letter), .\wire (light2_1_wire));
  Light2 light2_4 (
    .end_game(or_1_out), .ASCII(7'b1010000), .letter_button(in_16), .light(out_67),
    .latest_letter(light2_1_latest_letter), .\wire (light2_1_wire));
  Light2 light2_5 (
    .end_game(or_1_out), .ASCII(7'b1010101), .letter_button(in_21), .light(out_72),
    .latest_letter(light2_1_latest_letter), .\wire (light2_1_wire));
  Light2 light2_6 (
    .end_game(or_1_out), .ASCII(7'b1000010), .letter_button(in_2), .light(out_39),
    .latest_letter(light2_1_latest_letter), .\wire (light2_1_wire));
  Light2 light2_7 (
    .end_game(or_1_out), .ASCII(7'b1000111), .letter_button(in_7), .light(out_44),
    .latest_letter(light2_1_latest_letter), .\wire (light2_1_wire));
  Light2 light2_8 (
    .end_game(or_1_out), .ASCII(7'b1001100), .letter_button(in_12), .light(out_57),
    .latest_letter(light2_1_latest_letter), .\wire (light2_1_wire));
  Light2 light2_9 (
    .end_game(or_1_out), .ASCII(7'b1010001), .letter_button(in_17), .light(out_68),
    .latest_letter(light2_1_latest_letter), .\wire (light2_1_wire));
  Light2 light2_10 (
    .end_game(or_1_out), .ASCII(7'b1010110), .letter_button(in_22), .light(out_73),
    .latest_letter(light2_1_latest_letter), .\wire (light2_1_wire));
  Light2 light2_11 (
    .end_game(or_1_out), .ASCII(7'b1000011), .letter_button(in_3), .light(out_40),
    .latest_letter(light2_1_latest_letter), .\wire (light2_1_wire));
  Light2 light2_12 (
    .end_game(or_1_out), .ASCII(7'b1001000), .letter_button(in_8), .light(out_45),
    .latest_letter(light2_1_latest_letter), .\wire (light2_1_wire));
  Light2 light2_13 (
    .end_game(or_1_out), .ASCII(7'b1001101), .letter_button(in_13), .light(out_58),
    .latest_letter(light2_1_latest_letter), .\wire (light2_1_wire));
  Light2 light2_14 (
    .end_game(or_1_out), .ASCII(7'b1010010), .letter_button(in_18), .light(out_69),
    .latest_letter(light2_1_latest_letter), .\wire (light2_1_wire));
  Light2 light2_15 (
    .end_game(or_1_out), .ASCII(7'b1010111), .letter_button(in_23), .light(out_74),
    .latest_letter(light2_1_latest_letter), .\wire (light2_1_wire));
  not not_2 (buttoon_pressed, not_3_out);
  not not_3 (not_3_out, light2_1_wire);
  Light2 light2_16 (
    .end_game(or_1_out), .ASCII(7'b1000100), .letter_button(in_4), .light(out_41),
    .latest_letter(light2_1_latest_letter), .\wire (light2_1_wire));
  Light2 light2_17 (
    .end_game(or_1_out), .ASCII(7'b1001001), .letter_button(in_9), .light(out_46),
    .latest_letter(light2_1_latest_letter), .\wire (light2_1_wire));
  Light2 light2_18 (
    .end_game(or_1_out), .ASCII(7'b1001110), .letter_button(in_14), .light(out_59),
    .latest_letter(light2_1_latest_letter), .\wire (light2_1_wire));
  Light2 light2_19 (
    .end_game(or_1_out), .ASCII(7'b1010011), .letter_button(in_19), .light(out_70),
    .latest_letter(light2_1_latest_letter), .\wire (light2_1_wire));
  Light2 light2_20 (
    .end_game(or_1_out), .ASCII(7'b1011000), .letter_button(in_24), .light(out_75),
    .latest_letter(light2_1_latest_letter), .\wire (light2_1_wire));
  Light2 light2_21 (
    .end_game(or_1_out), .ASCII(7'b1000101), .letter_button(in_5), .light(out_42),
    .latest_letter(light2_1_latest_letter), .\wire (light2_1_wire));
  Light2 light2_22 (
    .end_game(or_1_out), .ASCII(7'b1001010), .letter_button(in_10), .light(out_47),
    .latest_letter(light2_1_latest_letter), .\wire (light2_1_wire));
  Light2 light2_23 (
    .end_game(or_1_out), .ASCII(7'b1001111), .letter_button(in_15), .light(out_60),
    .latest_letter(light2_1_latest_letter), .\wire (light2_1_wire));
  Light2 light2_24 (
    .end_game(or_1_out), .ASCII(7'b1010100), .letter_button(in_20), .light(out_71),
    .latest_letter(light2_1_latest_letter), .\wire (light2_1_wire));
  Light2 light2_25 (
    .end_game(or_1_out), .ASCII(7'b1011001), .letter_button(in_25), .light(out_76),
    .latest_letter(light2_1_latest_letter), .\wire (light2_1_wire));
  Pull_Resistor #(.pull(1)) pull_resistor_1 (.node(light2_1_wire));
  Light2 light2_26 (
    .end_game(or_1_out), .ASCII(7'b1011010), .letter_button(in_26), .light(out_77),
    .latest_letter(light2_1_latest_letter), .\wire (light2_1_wire));
  gallows gallows_1 (
    .bus_0(WRONG_GUESSES), .Col_0_out(out_55), .Col_0_out_2(out_52), .Col_0_out_3(out_63),
    .Col_1_out(out_48), .Col_1_out_2(out_53), .Col_1_out_3(out_64), .Col_2_out(out_49), .Col_2_out_2(out_54),
    .Col_2_out_3(out_65), .Col_3_out(out_50), .Col_3_out_2(out_61), .Col_3_out_3(out_66), .Col_4_out(out_51),
    .Col_4_out_2(out_62));
  or or_2 (out_94, new_game, END_GAME);
  Display display_1 (
    .ASCII_code_out(out_89), .ASCII_code_out_2(out_82), .ASCII_code_out_3(out_83), .ASCII_code_out_4(out_84),
    .ASCII_code_out_5(out_85), .ASCII_code_out_6(out_86), .ASCII_code_out_7(out_87),
    .ASCII_code_out_8(out_88), .button_pressed(buttoon_pressed), .end_game(END_GAME), .new_game(new_game),
    .\matches (Matches), .letter_code_7(letter_code));
  wins wins_1 (.correct_pattern(Correct_pattern), .end_game(END_GAME), .Wins(out_78));
  or or_3 (new_game, START_prime, yes_button);
  and and_1 (END_GAME, no_button, xor_2_out);
  losses losses_1 (.Wrong_guesses(WRONG_GUESSES), .end_game(END_GAME), .losses(out_79));
  xor xor_2 (xor_2_out, LOSES, WIN);

  assign NO = no_button;
  assign out_92 = TTY;
  assign out_93 = tick_TTY;
  assign YES = yes_button;

  // Other names for the same wires on the sheet: Button_pressed = buttoon_pressed
endmodule
